# Fritzing sketch Week1A2 (saved by Fritzing 0.9.5d)
breadboards: 1

parts:
  VCC1 = Battery block 9V
  S1 = SWITCH-MOMENTARY-2 [package=tactile-switch-1101ne]  # not connected
  S2 = Pushbutton [package=THT]
  R1 = Resistor [tolerance=±5% resistance=220 package=THT]
  LED1 = LED - 5mm [color="Red (633nm)" package="5 mm [THT]"]
  LED2 = LED - 5mm [color="Red (633nm)" package="5 mm [THT]"]

nets:
  N1: VCC1.-, LED1.cathode
  N2: VCC1.+, S2.leg1
  N3: S2.leg0, R1.Pin_1
  N4: R1.Pin_0, LED2.anode
  N5: LED1.anode, LED2.cathode
